# Fritzing sketch Flask-RPi (saved by Fritzing 0.9.3b)
breadboards: 1

parts:
  R1 = Resistor [tolerance=±5% resistance=330 package=THT]
  LED1 = LED - 5mm [color="Red (633nm)" package="5 mm [THT]"]
  Raspberry_Pi_1 = Raspberry Pi 3 [part_number=RPI-3-V1.2]
  LED2 = LED - 5mm [color="Yellow (595nm)" package="5 mm [THT]"]
  R2 = Resistor [tolerance=±5% resistance=330 package=THT]
  LED3 = LED - 5mm [color="Green (560nm)" package="5 mm [THT]"]
  R3 = Resistor [tolerance=±5% resistance=330 package=THT]
  S1 = Pushbutton [package="[THT]"]
  R4 = Resistor [tolerance=±5% resistance=330 package=THT]
  PIR2 = PIR sensor

nets:
  N1: R1.Pin_0, LED1.cathode
  GND: R1.Pin_1, Raspberry_Pi_1.GND, R2.Pin_1, R3.Pin_1, R4.Pin_1, PIR2.GND
  N2: LED1.anode, Raspberry_Pi_1.GIPO13
  3V3: Raspberry_Pi_1.3v3, S1.Pin_3, S1.Pin_4, PIR2.VDD
  N3: Raspberry_Pi_1.GIPO19, LED2.anode
  N4: Raspberry_Pi_1.GIPO26, LED3.anode
  N5: Raspberry_Pi_1.GIPO20, S1.Pin_1, S1.Pin_2, R4.Pin_0
  N6: Raspberry_Pi_1.GIPO16, PIR2.SIG
  N7: LED2.cathode, R2.Pin_0
  N8: LED3.cathode, R3.Pin_0

notes:
  GPIO 13
  GPIO 19
  GPIO 20
  GPIO 26
  3.3V
  GPIO 16
